# Fritzing sketch Untitled Sketch (saved by Fritzing 0.9.3b)
breadboards: 1

parts:
  Componente1 = Arduino Uno (Rev3)
  DI1 = 7-Segment LED Display [package=THT]
  DI2 = 7-Segment LED Display [package=THT]
  T1 = LM35 Temperature Sensor [package="TO92 [THT]"]

nets:
  N1: Componente1.A0, T1.Vout
  N2: Componente1.D8, DI2.cathodeF
  N3: Componente1.D9_PWM, DI2.commAnode#2
  N4: Componente1.D10_PWM/SS, DI1.commAnode#2
  N5: Componente1.D2, DI1.cathodeA, DI2.cathodeA
  N6: Componente1.D3_PWM, DI1.cathodeB, DI2.cathodeB
  N7: Componente1.D4, DI1.cathodeC, DI2.cathodeC
  N8: Componente1.D5_PWM, DI2.cathodeD
  N9: Componente1.D6_PWM, DI2.cathodeE
  N10: Componente1.D7, DI2.cathodeG
  N11: Componente1.5V, T1.+Vs
  GND: Componente1.GND, T1.GND

// code stored in the sketch: lm35_com_display_bcd.ino

////////// matriz display
int saidas[]={2,3,4,5,6,7,8,9,10};
              // a b c d e f g
int pinos[10][7]= {
    //  letras    a,b,c,d,e,f,g  
                 {1,1,1,1,1,1,0}, //0
                 {0,1,1,0,0,0,0}, //1
                 {1,1,0,1,1,0,1}, //2
                 {1,1,1,1,0,0,1}, //3
                 {0,1,1,0,0,1,1}, //4
                 {1,0,1,1,0,1,1}, //5
                 {1,0,1,1,1,1,1}, //6
                 {1,1,1,0,0,0,0}, //7
                 {1,1,1,1,1,1,1}, //8
                 {1,1,1,1,0,1,1}  //9                           
};



const int LM35 = A0; // Define o pino que lera a saída do LM35
float temperatura; // Variável que armazenará a temperatura medida
 
//Função que será executada uma vez quando ligar ou resetar o Arduino
void setup() {
Serial.begin(9600); // inicializa a comunicação serial
for (int i=0;i<11;i++){
  pinMode(saidas[i],OUTPUT);
}

}
 
void loop() {
//float leitura=analogRead(LM35);
temperatura = (float(analogRead(LM35))*5/(1023))/0.01;
delay(1);
/*Serial.print("Temperatura: ");
//Serial.println(temperatura);
Serial.print("LEITURA NA ENTRADA: ");
Serial.println(leitura); 
//delay(2000);
*/
int dezena= temperatura/10;

 Serial.print("dezena: ");
 Serial.println(dezena);
int unidade = temperatura-(dezena*10) ;


Serial.print("unidade: ");
 Serial.println(unidade);
   ///////////////display/////
   ///////////dezena
  digitalWrite(2,pinos[dezena][0]);
  digitalWrite(3,pinos[dezena][1]);
  digitalWrite(4,pinos[dezena][2]);
  digitalWrite(5,pinos[dezena][3]);
  digitalWrite(6,pinos[dezena][4]);
  digitalWrite(7,pinos[dezena][5]);
  digitalWrite(8,pinos[dezena][6]);
  digitalWrite(9,0);
  digitalWrite(10,1);
  delay(1);
  //////////unidade
  digitalWrite(10,1);
  digitalWrite(9,1);
  delayMicroseconds(2000);
  ////////////////////////// 
  digitalWrite(2,pinos[unidade][0]);
  digitalWrite(3,pinos[unidade][1]);
  digitalWrite(4,pinos[unidade][2]);
  digitalWrite(5,pinos[unidade][3]);
  digitalWrite(6,pinos[unidade][4]);
  digitalWrite(7,pinos[unidade][5]);
  digitalWrite(8,pinos[unidade][6]);
  digitalWrite(10,0);
  digitalWrite(9,1);
  delayMicroseconds(2000);
  //////////////////////////
  digitalWrite(10,1);
  digitalWrite(9,1);
  delayMicroseconds(2000);
  
   
}

// code stored in the sketch: Untitled.ino


////////// matriz display
  int saidas[]={2,3,4,5,6,7,8,9,10,};
              // a b c d e f g
int pinos[10][7]= {
    //  letras    a,b,c,d,e,f,g  
                 {1,1,1,1,1,1,0}, //0
                 {0,1,1,0,0,0,0}, //1
                 {1,1,0,1,1,0,1}, //2
                 {1,1,1,1,0,0,1}, //3
                 {0,1,1,0,0,1,1}, //4
                 {1,0,1,1,0,1,1}, //5
                 {1,0,1,1,1,1,1}, //6
                 {1,1,1,0,0,0,0}, //7
                 {1,1,1,1,1,1,1}, //8
                 {1,1,1,1,0,1,1}  //9                           
};




const int LM35 = A0; // Define o pino que lera a saída do LM35
float temperatura; // Variável que armazenará a temperatura medida
 
//Função que será executada uma vez quando ligar ou resetar o Arduino
void setup() {
Serial.begin(9600); // inicializa a comunicação serial
for (int i=0;i<11;i++){
  pinMode(saidas[i],OUTPUT);
}


}
 
void loop() {
//float leitura=analogRead(LM35);
temperatura = (float(analogRead(LM35))*5/(1023))/0.01;
delay(1);
/*Serial.print("Temperatura: ");
//Serial.println(temperatura);
Serial.print("LEITURA NA ENTRADA: ");
Serial.println(leitura); 
//delay(2000);
*/
int dezena= temperatura/10;


 Serial.print("dezena: ");
 Serial.println(dezena);
int unidade = temperatura-(dezena*10) ;



Serial.print("unidade: ");
 Serial.println(unidade);
   ///////////////display/////
   ///////////dezena
  digitalWrite(2,pinos[dezena][0]);
  digitalWrite(3,pinos[dezena][1]);
  digitalWrite(4,pinos[dezena][2]);
  digitalWrite(5,pinos[dezena][3]);
  digitalWrite(6,pinos[dezena][4]);
  digitalWrite(7,pinos[dezena][5]);
  digitalWrite(8,pinos[dezena][6]);
  digitalWrite(9,0);
  digitalWrite(10,1);
  delay(1);
  //////////unidade
  digitalWrite(10,1);
  digitalWrite(9,1);
  delayMicroseconds(2000);
  ////////////////////////// 
  digitalWrite(2,pinos[unidade][0]);
  digitalWrite(3,pinos[unidade][1]);
  digitalWrite(4,pinos[unidade][2]);
  digitalWrite(5,pinos[unidade][3]);
  digitalWrite(6,pinos[unidade][4]);
  digitalWrite(7,pinos[unidade][5]);
  digitalWrite(8,pinos[unidade][6]);
  digitalWrite(10,0);
  digitalWrite(9,1);
  delayMicroseconds(2000);
  //////////////////////////
  digitalWrite(10,1);
  digitalWrite(9,1);
  delayMicroseconds(2000);
  
   
}
